# Fritzing sketch Schematic (saved by Fritzing 0.9.1b)

parts:
  Launchpad1 = TI Launchpad MSP430G2
  U1 = LCD-16X2 [package=lcd-16x2]  # not connected
  RE1 = Rotary Encoder [package=THT]
  S1 = Pushbutton [package="[THT]"]
  RE2 = Rotary Encoder [package=THT]
  S2 = Pushbutton [package="[THT]"]
  RE3 = Rotary Encoder [package=THT]
  S3 = Pushbutton [package="[THT]"]
  X2 = USB Connectors [package=usb-minib-nostop]  # not connected

nets:
  N1: Launchpad1.p10, RE3.EncoderPinB
  N2: Launchpad1.p9, RE3.EncoderPinA
  N3: Launchpad1.p8, RE2.EncoderPinB
  N4: Launchpad1.p7, RE2.EncoderPinA
  N5: Launchpad1.p6, RE1.EncoderPinB
  N6: Launchpad1.p5, RE1.EncoderPinA
  N7: Launchpad1.p4, Launchpad1.p3, Launchpad1.p2, Launchpad1.p20, RE1.EncoderPinC, S1.Pin_3, S1.Pin_4, RE2.EncoderPinC, S2.Pin_3, S2.Pin_4, RE3.EncoderPinC, S3.Pin_3, S3.Pin_4
